// Logisim project Ctl_Conditional.circ as structural Verilog: 1 circuit, main circuit Conditional
module Conditional (
  input  Enable,
  input  [15:0] Instruction,
  input  Z,
  input  C,
  input  N,
  input  V,
  output [10:0] Offset,
  output Verified
);

  wire and_1_out, and_2_out, and_3_out, and_5_out, Booleen_estCond, N_Diff_V, N_egal_V, not_1_out, not_2_out,
       not_3_out, not_4_out, not_5_out, not_6_out, not_7_out, not_8_out, or_1_out, or_2_out, Verif_out;
  wire [10:0] bit_extender_1_out, bit_extender_2_out, bit_extender_3_out, multiplexer_3_out, Offset_t;

  not not_1 (not_1_out, C);
  or or_1 (or_1_out, not_1_out, Z);
  not not_2 (not_2_out, Z);
  and and_1 (and_1_out, C, not_3_out);
  not not_3 (not_3_out, Z);
  and and_2 (and_2_out, not_2_out, N_egal_V);
  or or_2 (or_2_out, Z, N_Diff_V);
  not not_4 (not_4_out, Z);
  not not_5 (not_5_out, C);
  not not_6 (not_6_out, N);
  not not_7 (not_7_out, V);
  Multiplexer #(.select(4)) multiplexer_1 (
    .in0(Z), .in1(not_4_out), .in2(C), .in3(not_5_out), .in4(N), .in5(not_6_out), .in6(V), .in7(not_7_out),
    .in8(and_1_out), .in9(or_1_out), .in10(N_egal_V), .in11(N_Diff_V), .in12(and_2_out), .in13(or_2_out),
    .in14(1'b1), .in15(not_8_out), .out(Verif_out), .sel(Instruction[11:8]));
  not not_8 (not_8_out, 1'b1);
  assign bit_extender_1_out = {{10{Verified}}, Verified};  // Bit_Extender bit_extender_1
  and and_3 (and_3_out, Enable, 1'b1);
  assign Offset = Offset_t & bit_extender_1_out;  // AND_Gate and_4, 11 bits wide
  and and_5 (and_5_out, Enable, Verif_out);
  assign bit_extender_2_out = {{3{Instruction[7]}}, Instruction[7:0]};  // Bit_Extender bit_extender_2
  Multiplexer multiplexer_2 (.in0(and_3_out), .in1(and_5_out), .out(Verified), .sel(Booleen_estCond));
  xnor xnor_1 (N_egal_V, N, V);
  xor xor_1 (N_Diff_V, N, V);
  Comparator #(.width(4)) comparator_1 (.a(Instruction[15:12]), .b(4'b1101), .eq(Booleen_estCond));  // open: gt, lt
  Multiplexer #(.width(11)) multiplexer_3 (
    .in0(Instruction[10:0]), .in1(bit_extender_2_out), .out(multiplexer_3_out), .sel(Booleen_estCond));
  assign bit_extender_3_out = {{10{Enable}}, Enable};  // Bit_Extender bit_extender_3
  assign Offset_t = bit_extender_3_out & multiplexer_3_out;  // AND_Gate and_6, 11 bits wide

  // Other names for the same wires on the sheet: Imm8[7:0] = Instruction[7:0]; Imm11[10:0] = Instruction[10:0];
  //   Instr[15:0] = Instruction; OpCode[3:0] = Instruction[11:8]; CodeConditionnel[3:0] = Instruction[15:12]
endmodule
