// Logisim project Ctl_SP_Address.circ as structural Verilog: 1 circuit, main circuit SP_Address
module SP_Address (
  input  Enable,
  input  [31:0] Stack_Pointer,
  input  [15:0] Instruction,
  output [31:0] New_Stack_Pointer,
  output Write_Enable
);

  wire operation;
  wire [15:0] and_1_out, bit_extender_1_out;
  wire [31:0] adder_1_out, bit_extender_3_out, imm7, res, subtractor_1_out;

  assign bit_extender_1_out = {{15{Enable}}, Enable};  // Bit_Extender bit_extender_1
  Adder #(.width(32)) adder_1 (.a(imm7), .b(Stack_Pointer), .out(adder_1_out));  // open: cin, cout
  Subtractor #(.width(32)) subtractor_1 (.a(Stack_Pointer), .b(imm7), .out(subtractor_1_out));  // open: bin, bout
  assign {and_1_out[15:8], operation, and_1_out[6:0]} = Instruction & bit_extender_1_out;  // AND_Gate and_1, 16 bits wide
  Multiplexer #(.width(32)) multiplexer_1 (.in0(adder_1_out), .in1(subtractor_1_out), .out(res), .sel(operation));
  assign imm7 = {{25{1'b0}}, and_1_out[6:0]};  // Bit_Extender bit_extender_2
  assign bit_extender_3_out = {{31{Enable}}, Enable};  // Bit_Extender bit_extender_3
  assign New_Stack_Pointer = res & bit_extender_3_out;  // AND_Gate and_2, 32 bits wide

  assign Write_Enable = Enable;

  // Other names for the same wires on the sheet: SP[31:0] = Stack_Pointer

  // Notes on the sheet:
  //   Pull output low on Enable = 0
endmodule
