// Logisim project ALU.circ as structural Verilog: 1 circuit, main circuit ALU
module ALU (
  input  [31:0] A,
  input  [31:0] B,
  input  [4:0] Shift,
  input  [3:0] Codop,
  input  CarryIn,
  output [31:0] S,
  output [3:0] Flags
);

  wire bitselector_2_out, bitselector_3_out, bitselector_4_out, bitselector_5_out, bitselector_6_out,
       bitselector_7_out, bitselector_8_out, bitselector_11_out, bitselector_12_out, bitselector_13_out,
       bitselector_14_out, comparator_2_eq, comparator_3_eq, comparator_4_eq, comparator_5_eq,
       comparator_6_eq, comparator_7_eq, comparator_8_eq, comparator_9_eq, comparator_10_eq, Cout1, Cout2,
       Cout3, Cout4, LSL, LSR, N_out, not_1_out, not_6_out, not_7_out, not_8_out, not_9_out, not_10_out,
       subtractor_1_bout, subtractor_3_bout, VadcCMN, VsbcAseul, VsbcCMP, Z_out;
  wire [4:0] adder_3_out, subtractor_4_out;
  wire [31:0] Add, and_1_out, and_3_out, CMN, CMP, multiplier_1_out, not_2_out, not_5_out, or_1_out,
       shifter_1_out, shifter_2_out, shifter_3_out, shifter_4_out, subtractor_1_out, subtractor_2_out, TST,
       xor_1_out;

  not not_1 (not_1_out, CarryIn);
  assign not_2_out = ~A;  // NOT_Gate not_2, 32 bits wide
  assign and_1_out = A & B;  // AND_Gate and_1, 32 bits wide
  assign xor_1_out = A ^ B;  // XOR_Gate xor_1, 32 bits wide
  Shifter #(.width(32)) shifter_1 (.in(B), .\dist (Shift), .out(shifter_1_out));
  Shifter #(.shift("lr"), .width(32)) shifter_2 (.in(B), .\dist (Shift), .out(shifter_2_out));
  Shifter #(.shift("ar"), .width(32)) shifter_3 (.in(B), .\dist (Shift), .out(shifter_3_out));
  Adder #(.width(32)) adder_1 (.a(A), .b(B), .out(Add), .cin(CarryIn), .cout(Cout1));
  Subtractor #(.width(32)) subtractor_1 (
    .a(B), .b(A), .out(subtractor_1_out), .bin(not_1_out), .bout(subtractor_1_bout));
  not not_3 (Cout2, subtractor_1_bout);
  Shifter #(.shift("rr"), .width(32)) shifter_4 (.in(B), .\dist (Shift), .out(shifter_4_out));
  assign TST = A & B;  // AND_Gate and_2, 32 bits wide
  Subtractor #(.width(32)) subtractor_2 (.a({32{1'b0}}), .b(A), .out(subtractor_2_out));  // open: bin, bout
  Subtractor #(.width(32)) subtractor_3 (.a(B), .b(A), .out(CMP), .bout(subtractor_3_bout));  // open: bin
  not not_4 (Cout3, subtractor_3_bout);
  Adder #(.width(32)) adder_2 (.a(B), .b(A), .out(CMN), .cout(Cout4));  // open: cin
  assign or_1_out = B | A;  // OR_Gate or_1, 32 bits wide
  Multiplier #(.width(32)) multiplier_1 (.a(B), .b(A), .out(multiplier_1_out));  // open: cin, cout
  assign and_3_out = B & not_2_out;  // AND_Gate and_3, 32 bits wide
  assign not_5_out = ~A;  // NOT_Gate not_5, 32 bits wide
  Multiplexer #(.select(4), .width(32)) multiplexer_1 (
    .in0(and_1_out), .in1(xor_1_out), .in2(shifter_1_out), .in3(shifter_2_out), .in4(shifter_3_out),
    .in5(Add), .in6(subtractor_1_out), .in7(shifter_4_out), .in8(B), .in9(subtractor_2_out), .in10(B),
    .in11(B), .in12(or_1_out), .in13(multiplier_1_out), .in14(and_3_out), .in15(not_5_out), .out(S),
    .sel(Codop));
  BitSelector #(.width(32)) bitselector_1 (.in(S), .out(N_out), .sel({5{1'b1}}));
  Comparator #(.width(32)) comparator_1 (.a(S), .b({32{1'b0}}), .eq(Z_out));  // open: gt, lt
  BitSelector #(.width(32)) bitselector_2 (.in(A), .out(bitselector_2_out), .sel({5{1'b1}}));
  BitSelector #(.width(32)) bitselector_3 (.in(B), .out(bitselector_3_out), .sel({5{1'b1}}));
  BitSelector #(.width(32)) bitselector_4 (.in(A), .out(bitselector_4_out), .sel({5{1'b1}}));
  Comparator #(.width(1)) comparator_2 (.a(bitselector_4_out), .b(N_out), .eq(comparator_2_eq));  // open: gt, lt
  BitSelector #(.width(32)) bitselector_5 (.in(A), .out(bitselector_5_out), .sel({5{1'b1}}));
  BitSelector #(.width(32)) bitselector_6 (.in(B), .out(bitselector_6_out), .sel({5{1'b1}}));
  BitSelector #(.width(32)) bitselector_7 (.in(B), .out(bitselector_7_out), .sel({5{1'b1}}));
  BitSelector #(.width(32)) bitselector_8 (.in(A), .out(bitselector_8_out), .sel({5{1'b1}}));
  Comparator #(.width(1)) comparator_3 (
    .a(bitselector_2_out), .b(bitselector_3_out), .eq(comparator_3_eq));  // open: gt, lt
  not not_6 (not_6_out, comparator_2_eq);
  Comparator #(.width(1)) comparator_4 (
    .a(bitselector_5_out), .b(bitselector_6_out), .eq(comparator_4_eq));  // open: gt, lt
  not not_7 (not_7_out, comparator_5_eq);
  Comparator #(.width(1)) comparator_5 (.a(bitselector_7_out), .b(N_out), .eq(comparator_5_eq));  // open: gt, lt
  Comparator #(.width(1)) comparator_6 (.a(bitselector_8_out), .b(1'b0), .eq(comparator_6_eq));  // open: gt, lt
  not not_8 (not_8_out, comparator_7_eq);
  Comparator #(.width(1)) comparator_7 (.a(1'b0), .b(N_out), .eq(comparator_7_eq));  // open: gt, lt
  and and_4 (VadcCMN, comparator_3_eq, not_6_out);
  not not_9 (not_9_out, comparator_4_eq);
  and and_5 (VsbcCMP, not_9_out, not_7_out);
  not not_10 (not_10_out, comparator_6_eq);
  and and_6 (VsbcAseul, not_10_out, not_8_out);
  BitSelector #(.width(32)) bitselector_9 (.in(B), .out(LSL), .sel(adder_3_out));
  Adder #(.width(5)) adder_3 (.a(Shift), .b(5'b00001), .out(adder_3_out));  // open: cin, cout
  BitSelector #(.width(32)) bitselector_10 (.in(B), .out(LSR), .sel(subtractor_4_out));
  Subtractor #(.width(5)) subtractor_4 (.a(Shift), .b(5'b00001), .out(subtractor_4_out));  // open: bin, bout
  BitSelector #(.width(32)) bitselector_11 (.in(TST), .out(bitselector_11_out), .sel({5{1'b1}}));
  BitSelector #(.width(32)) bitselector_12 (.in(CMP), .out(bitselector_12_out), .sel({5{1'b1}}));
  BitSelector #(.width(32)) bitselector_13 (.in(CMN), .out(bitselector_13_out), .sel({5{1'b1}}));
  Comparator #(.width(32)) comparator_8 (.a(TST), .b({32{1'b0}}), .eq(comparator_8_eq));  // open: gt, lt
  Comparator #(.width(32)) comparator_9 (.a(CMP), .b({32{1'b0}}), .eq(comparator_9_eq));  // open: gt, lt
  Comparator #(.width(32)) comparator_10 (.a(CMN), .b({32{1'b0}}), .eq(comparator_10_eq));  // open: gt, lt
  BitSelector #(.width(32)) bitselector_14 (.in(B), .out(bitselector_14_out), .sel({5{1'b1}}));
  Multiplexer #(.select(4)) multiplexer_2 (
    .in0(1'b0), .in1(1'b0), .in2(LSL), .in3(LSR), .in4(LSR), .in5(Cout1), .in6(Cout2),
    .in7(bitselector_14_out), .in8(1'b0), .in9(1'b0), .in10(Cout3), .in11(Cout4), .in12(1'b0), .in13(1'b0),
    .in14(1'b0), .in15(1'b0), .out(Flags[1]), .sel(Codop));
  Multiplexer #(.select(4)) multiplexer_3 (
    .in0(N_out), .in1(N_out), .in2(N_out), .in3(N_out), .in4(N_out), .in5(N_out), .in6(N_out), .in7(N_out),
    .in8(bitselector_11_out), .in9(N_out), .in10(bitselector_12_out), .in11(bitselector_13_out),
    .in12(N_out), .in13(N_out), .in14(N_out), .in15(N_out), .out(Flags[3]), .sel(Codop));
  Multiplexer #(.select(4)) multiplexer_4 (
    .in0(Z_out), .in1(Z_out), .in2(Z_out), .in3(Z_out), .in4(Z_out), .in5(Z_out), .in6(Z_out), .in7(Z_out),
    .in8(comparator_8_eq), .in9(Z_out), .in10(comparator_9_eq), .in11(comparator_10_eq), .in12(Z_out),
    .in13(Z_out), .in14(Z_out), .in15(Z_out), .out(Flags[2]), .sel(Codop));
  Multiplexer #(.select(4)) multiplexer_5 (
    .in0(1'b0), .in1(1'b0), .in2(1'b0), .in3(1'b0), .in4(1'b0), .in5(VadcCMN), .in6(VsbcCMP), .in7(1'b0),
    .in8(1'b0), .in9(VsbcAseul), .in10(VsbcCMP), .in11(VadcCMN), .in12(1'b0), .in13(1'b0), .in14(1'b0),
    .in15(1'b0), .out(Flags[0]), .sel(Codop));

  // Other names for the same wires on the sheet: V = Flags[0]; C = Flags[1]; Z = Flags[2]; N = Flags[3];
  //   Res[31:0] = S

  // Notes on the sheet:
  //   Note: for ROR, C = N
  //   Note 2: assume that shift > 0 for LSL and LSR
endmodule
