// Logisim project Ctl_Load_Store.circ as structural Verilog: 1 circuit, main circuit Load_Store
module Load_Store (
  input  Enable,
  input  [15:0] Instruction,
  input  Clk,
  input  Reset,
  input  [31:0] Stack_Pointer,
  output Store,
  output Load,
  output PC_Hold,
  output [2:0] Rmd,
  output [31:0] RAM_Addr
);

  wire d_ff_1_q, Instr11eBit, Load_Store, not_1_out, xor_1_out;
  wire [2:0] bit_extender_2_out, bit_extender_3_out;
  wire [3:0] bitselector_3_out;
  wire [7:0] bitselector_1_out;
  wire [31:0] adder_1_out, bit_extender_4_out, imm8;

  BitSelector #(.group(8), .width(16)) bitselector_1 (.in(Instruction), .out(bitselector_1_out), .sel(1'b0));
  assign imm8 = {{24{bitselector_1_out[7]}}, bitselector_1_out};  // Bit_Extender bit_extender_1
  BitSelector #(.width(16)) bitselector_2 (.in(Instruction), .out(Instr11eBit), .sel(4'b1011));
  and and_1 (Load_Store, Instr11eBit, 1'b1);
  Adder #(.width(32)) adder_1 (.a(imm8), .b(Stack_Pointer), .out(adder_1_out));  // open: cin, cout
  and and_2 (Load, Load_Store, Enable);
  not not_1 (not_1_out, Load_Store);
  BitSelector #(.group(4), .width(16)) bitselector_3 (.in(Instruction), .out(bitselector_3_out), .sel(2'b10));
  and and_3 (Store, not_1_out, Enable);
  assign bit_extender_2_out = {{2{Enable}}, Enable};  // Bit_Extender bit_extender_2
  Bit_Extender #(.in_width(4), .out_width(3)) bit_extender_3 (.in(bitselector_3_out), .out(bit_extender_3_out));
  D_Flip_Flop d_ff_1 (.D(xor_1_out), .clk(Clk), .Q(d_ff_1_q), .reset(Reset));  // open: Qn, preset
  xor xor_1 (xor_1_out, d_ff_1_q, Load_Store);
  assign bit_extender_4_out = {{31{Enable}}, Enable};  // Bit_Extender bit_extender_4
  assign Rmd = bit_extender_2_out & bit_extender_3_out;  // AND_Gate and_4, 3 bits wide
  assign RAM_Addr = bit_extender_4_out & adder_1_out;  // AND_Gate and_5, 32 bits wide
  and and_6 (PC_Hold, Enable, d_ff_1_q);

  // Other names for the same wires on the sheet: Clock = Clk; Stack_P[31:0] = Stack_Pointer

  // Notes on the sheet:
  //   Instruction: pull=down
  //   Delay load and hold PC for 1 cycle for the RAM to send out requested data 
endmodule
