// Logisim project Ctl_Opcode_Decoder.circ as structural Verilog: 1 circuit, main circuit Opcode_Decoder
module Opcode_Decoder (
  input  [5:0] Opcode,
  output Shift,
  output Data_Processing,
  output Load_Store,
  output SP_Address,
  output Conditional
);

  wire and_5_out, and_6_out, not_1_out, not_2_out, not_3_out, not_4_out, not_5_out, not_6_out, not_7_out,
       not_8_out, not_9_out, not_10_out, not_11_out, not_12_out, not_13_out;

  not not_1 (not_1_out, Opcode[4]);
  not not_2 (not_2_out, Opcode[5]);
  not not_3 (not_3_out, Opcode[5]);
  not not_4 (not_4_out, Opcode[3]);
  not not_5 (not_5_out, Opcode[2]);
  not not_6 (not_6_out, Opcode[1]);
  not not_7 (not_7_out, Opcode[0]);
  not not_8 (not_8_out, Opcode[4]);
  and and_1 (Load_Store, Opcode[5], not_8_out, not_9_out, Opcode[2]);
  not not_9 (not_9_out, Opcode[3]);
  not not_10 (not_10_out, Opcode[4]);
  and and_2 (SP_Address, Opcode[5], not_10_out, Opcode[3], Opcode[2]);
  not not_11 (not_11_out, Opcode[3]);
  not not_12 (not_12_out, Opcode[2]);
  not not_13 (not_13_out, Opcode[1]);
  and and_3 (Shift, not_1_out, not_2_out);
  and and_4 (Data_Processing, not_3_out, Opcode[4], not_4_out, not_5_out, not_6_out, not_7_out);
  and and_5 (and_5_out, Opcode[5], Opcode[4], not_11_out, Opcode[2]);
  or or_1 (Conditional, and_5_out, and_6_out);
  and and_6 (and_6_out, Opcode[5], Opcode[4], Opcode[3], not_12_out, not_13_out);

  // Other names for the same wires on the sheet: f0 = Opcode[0]; f1 = Opcode[1]; f2 = Opcode[2]; f3 = Opcode[3];
  //   f4 = Opcode[4]; f5 = Opcode[5]

  // Notes on the sheet:
  //   Shift, add, sub, mov
  //   Load/Store
  //   SP Address
  //   Conditional branch
  //   Data Processing
endmodule
